# Fritzing sketch 1A_AC_TODC_PSU_k1823_compact (saved by Fritzing 1.0.1rc)
circuit board: 2.54656cm x 4.13825cm

parts:
  D3 = Rectifier Diode [part_number=1N4007 package="300 mil [THT]"]
  C2 = Capacitor [part_number=0.1uF package=cap-pth-small]
  D4 = Rectifier Diode [part_number=1N4007 package="300 mil [THT]"]
  C4 = Electrolytic Capacitor [capacitance=1µF voltage=35V package="100 mil [THT, electrolytic]"]
  R1 = Resistor [tolerance=±5% power=0.25W resistance=220 package=THT]
  U1 = Voltage Regulator - Variable [package="TO220 [THT]"]
  C1 = Electrolytic Capacitor [capacitance=2.2nF voltage=35V package="200 mil [THT, electrolytic]"]
  R3 = TRIMPOT [maximum_resistance=4.7kΩ knob_status=50% power=0.5W package=trimpot_pth_s3_lock]
  D2 = Rectifier Diode [part_number=1N4007 package="300 mil [THT]"]
  J2 = Camdenboss CTB0158-2 [part_number=CTB0158-2 package=THT]
  J1 = Camdenboss CTB0158-2 [part_number=CTB0158-2 package=THT]
  D1 = Rectifier Diode [part_number=1N4007 package="300 mil [THT]"]
  C3 = Electrolytic Capacitor [capacitance=10µF voltage=35V package="100 mil [THT, electrolytic]"]

nets:
  N1: D3.cathode, D4.anode, J1.pin1
  GND: D3.anode, C2.2, C4.-, C1.-, R3.WIPER, R3.CW, D2.anode, J2.pin2, C3.-
  N2: C2.1, D4.cathode, U1.IN, C1.+, D1.cathode
  N3: C4.+, R1.Pin_0, U1.OUT, J2.pin1
  N4: R1.Pin_1, U1.ADJ, R3.CCW, C3.+
  N5: D2.cathode, J1.pin2, D1.anode
